// Digital circuit Problem1.dig as structural Verilog
module Problem1 (
  input  [1:0] S,
  input  [3:0] A,
  output [3:0] X
);

  Multiplexer #(.Selector_Bits(2)) multiplexer_1 (
    .sel(S), .in_0(A[0]), .in_1(1'b0), .in_2(1'b0), .in_3(1'b0), .out(X[0]));
  Multiplexer #(.Selector_Bits(2)) multiplexer_2 (
    .sel(S), .in_0(A[1]), .in_1(A[0]), .in_2(1'b0), .in_3(1'b0), .out(X[1]));
  Multiplexer #(.Selector_Bits(2)) multiplexer_3 (
    .sel(S), .in_0(A[2]), .in_1(A[1]), .in_2(A[0]), .in_3(1'b0), .out(X[2]));
  Multiplexer #(.Selector_Bits(2)) multiplexer_4 (
    .sel(S), .in_0(A[3]), .in_1(A[2]), .in_2(A[1]), .in_3(A[0]), .out(X[3]));
endmodule

/* Test case Grader:
		A S X
loop(i,4)
	repeat(16) (n)	(i)	(n << i)
end loop
*/
