// Digital circuit Problem2.dig as structural Verilog
module Problem2 (
  input  Reset,
  input  C,
  output X_0,
  output X_1,
  output X_2,
  output X_3
);

  wire [0:0] nand_1_out;
  wire [3:0] add_1_s, multiplexer_1_out;

  Multiplexer #(.Bits(4)) multiplexer_1 (.sel(Reset), .in_0(add_1_s), .in_1(4'b0000), .out(multiplexer_1_out));
  D_FF #(.Bits(4)) d_ff_1 (.D(multiplexer_1_out), .C(C), .Q({X_3, X_2, X_1, X_0}));  // open: nQ
  Add #(.Bits(4)) add_1 (.a({3'b000, nand_1_out[0]}), .b({X_3, X_2, X_1, X_0}), .c_i(1'b0), .s(add_1_s));  // open: c_o
  nand nand_1 (nand_1_out[0], X_0, X_1, X_2, X_3);
endmodule

/* Test case Grader:
C	Reset	X_3 X_2 X_1 X_0
0 0 0 0 0 0
loop(i, 15)
	C 0 bits(4, i + 1)
end loop
	C 0 1 1 1 1
	C 0 1 1 1 1
*/
