// Digital circuit Problem3.dig as structural Verilog
module Problem3 (
  input  WE,
  input  [1:0] S,
  input  [3:0] A,
  input  C,
  output [3:0] X
);

  wire demultiplexer_1_out_0, demultiplexer_1_out_1, demultiplexer_1_out_2, demultiplexer_1_out_3;
  wire [3:0] register_1_q, register_2_q, register_3_q, register_4_q;

  Demultiplexer #(.Selector_Bits(2)) demultiplexer_1 (
    .sel(S), .in(WE), .out_0(demultiplexer_1_out_0), .out_1(demultiplexer_1_out_1),
    .out_2(demultiplexer_1_out_2), .out_3(demultiplexer_1_out_3));
  Register #(.Bits(4)) register_1 (.D(A), .C(C), .en(demultiplexer_1_out_0), .Q(register_1_q));
  Register #(.Bits(4)) register_2 (.D(A), .C(C), .en(demultiplexer_1_out_1), .Q(register_2_q));
  Register #(.Bits(4)) register_3 (.D(A), .C(C), .en(demultiplexer_1_out_2), .Q(register_3_q));
  Register #(.Bits(4)) register_4 (.D(A), .C(C), .en(demultiplexer_1_out_3), .Q(register_4_q));
  Multiplexer #(.Bits(4), .Selector_Bits(2)) multiplexer_1 (
    .sel(S), .in_0(register_1_q), .in_1(register_2_q), .in_2(register_3_q), .in_3(register_4_q), .out(X));
endmodule

/* Test case Grader:
A S C WE X
0 0 0 0  0
loop(i, 16)
loop(j, 4)
	(i) (j) C 0 0
end loop
end loop	
0 0 0 1 0
loop(i, 4)
loop(j, 16)
	(j) (i) C 1 (j)
	(j) (i) C 0 (j)
	(0) (i) C 0 (j)
end loop
end loop
loop(i, 4)
	0 (i) C 1 0
end loop
0 0 0 0  0
2 0 0 1  0
2 0 1 1  2
2 0 0 1  2
1 1 0 1  0
1 1 1 1  1
1 1 0 1  1
3 2 0 1  0
3 2 1 1  3
0 3 0 1  0
0 3 1 1  0
0 3 0 1  0
0 0 0 0  2
0 1 0 0  1
0 2 0 0  3
0 3 0 0  0
*/
